# Fritzing sketch RPi-bigboard (saved by Fritzing 0.9.3b)
breadboards: 1

parts:
  Raspberry_Pi_1 = Raspberry Pi 3 [part_number=RPI-3-V1.2]
  LED1 = smd LED [color="Red (633nm)" package="1206 [SMD]"]
  LED2 = smd LED [color="Yellow (595nm)" package="1206 [SMD]"]
  LED3 = smd LED [color="Green (565nm)" package="1206 [SMD]"]
  LED4 = smd LED [color="Red (633nm)" package="1206 [SMD]"]
  LED5 = smd LED [color="Green (565nm)" package="1206 [SMD]"]
  R2 = Resistor [tolerance=±1% resistance=150 package=THT]
  R3 = Resistor [tolerance=±1% resistance=150 package=THT]
  LED7 = smd LED [color="Red (633nm)" package="1206 [SMD]"]
  R4 = Resistor [tolerance=±1% resistance=150 package=THT]
  R5 = Resistor [tolerance=±1% resistance=150 package=THT]
  R6 = Resistor [tolerance=±1% resistance=150 package=THT]
  R7 = Resistor [tolerance=±1% resistance=150 package=THT]
  R8 = Resistor [tolerance=±1% resistance=150 package=THT]
  S2 = Pushbutton [package="[THT]"]
  S3 = Pushbutton [package="[THT]"]
  LED6 = smd LED [color="Red (633nm)" package="1206 [SMD]"]

nets:
  N1: Raspberry_Pi_1.GPIO4, S3.Pin_3, S3.Pin_4
  N2: Raspberry_Pi_1.GPIO17, LED1.anode
  N3: Raspberry_Pi_1.GPIO27, LED2.anode
  N4: Raspberry_Pi_1.GPIO22, LED3.anode
  N5: Raspberry_Pi_1.GPIO9, S2.Pin_3, S2.Pin_4
  N6: Raspberry_Pi_1.GND, R2.Pin_1, R3.Pin_1, R4.Pin_1, R5.Pin_1, R6.Pin_1, R7.Pin_1, R8.Pin_1, S2.Pin_1, S2.Pin_2, S3.Pin_1, S3.Pin_2
  N7: Raspberry_Pi_1.GPIO25, LED7.anode
  N8: Raspberry_Pi_1.GPIO24, LED6.anode
  N9: Raspberry_Pi_1.GPIO23, LED5.anode
  N10: Raspberry_Pi_1.GPIO18, LED4.anode
  N11: LED1.cathode, R2.Pin_0
  N12: LED2.cathode, R3.Pin_0
  N13: LED3.cathode, R4.Pin_0
  N14: LED4.cathode, R5.Pin_0
  N15: LED5.cathode, R6.Pin_0
  N16: LED7.cathode, R8.Pin_0
  N17: R7.Pin_0, LED6.cathode

notes:
  traffic lights for cars
  traffic lights for human
  wait
  press
  press to turn green
  press to change sound
